// Logisim project 16 bit MIPS Architechture.circ as structural Verilog: 6 circuits, main circuit main
module main (
  input  [15:0] in_1,
  input  Enable,
  input  Clear,
  input  [3:0] in_4,
  input  [3:0] in_5,
  input  [3:0] in_6,
  input  [15:0] in_7,
  input  in_8,
  input  in_9,
  input  in_10,
  input  in_11,
  input  in_12,
  input  [15:0] in_13,
  input  [15:0] in_14,
  input  in_15,
  input  in_16,
  input  [15:0] in_17,
  input  [15:0] in_18,
  input  [1:0] in_19,
  input  [1:0] in_20,
  input  [1:0] in_21,
  output [15:0] out_22,
  output [15:0] out_23,
  output [15:0] out_24,
  output [15:0] out_25,
  output [15:0] out_26,
  output out_27,
  output out_28,
  output out_29,
  output out_30,
  output out_31,
  output out_32
);

  wire clock_1_out, clock_2_out;

  Clock clock_1 (.out(clock_1_out));
  Register #(.width(16)) register_1 (.D(in_1), .en(Enable), .Q(out_22), .clk(clock_1_out), .clr(Clear));
  Clock clock_2 (.out(clock_2_out));
  _1_bit_ALU u_1_bit_alu_1 (.ALU_Select(in_20), .Result(out_28), .Cout(out_30), .A(in_15), .B(in_16), .Cin(in_12));
  _16_bit_Register u_16_bit_register_1 (
    .Rs(in_4), .Rt(in_5), .Rd(in_6), .in_4(in_7), .write_Control(in_8), .out_8(out_23), .out_9(out_24),
    .Clear(in_9), .Clk(clock_2_out));
  _16_bit_ALU u_16_bit_alu_1 (
    .Cin(in_11), .ALU_Select(in_21), .Cout(out_32), .B(in_18), .A(in_14), .Result(out_26));  // open: Zero_Flag, Over_Flow
  _16_bit_ALU u_16_bit_alu_2 (
    .Cin(in_10), .ALU_Select(in_19), .Cout(out_31), .B(in_17), .A(in_13), .Result(out_25),
    .Zero_Flag(out_27), .Over_Flow(out_29));

  // Notes on the sheet:
  //   Input
  //   Clk
  //   Output
endmodule

module _16_bit_Register (
  input  [3:0] Rs,
  input  [3:0] Rt,
  input  [3:0] Rd,
  input  [15:0] in_4,
  input  write_Control,
  input  Clk,
  input  Clear,
  output [15:0] out_8,
  output [15:0] out_9
);

  wire and_1_out, and_2_out, and_3_out, and_4_out, and_5_out, and_6_out, and_7_out, and_8_out, and_9_out,
       and_10_out, and_11_out, and_12_out, and_13_out, and_14_out, and_15_out, and_16_out, decoder_1_out0,
       decoder_1_out1, decoder_1_out2, decoder_1_out3, decoder_1_out4, decoder_1_out5, decoder_1_out6,
       decoder_1_out7, decoder_1_out8, decoder_1_out9, decoder_1_out10, decoder_1_out11, decoder_1_out12,
       decoder_1_out13, decoder_1_out14, decoder_1_out15;
  wire [15:0] register_1_q, register_2_q, register_3_q, register_4_q, register_5_q, register_6_q,
       register_7_q, register_8_q, register_9_q, register_10_q, register_11_q, register_12_q, register_13_q,
       register_14_q, register_15_q, register_16_q;

  Decoder #(.select(4)) decoder_1 (
    .out0(decoder_1_out0), .out1(decoder_1_out1), .out2(decoder_1_out2), .out3(decoder_1_out3),
    .out4(decoder_1_out4), .out5(decoder_1_out5), .out6(decoder_1_out6), .out7(decoder_1_out7),
    .out8(decoder_1_out8), .out9(decoder_1_out9), .out10(decoder_1_out10), .out11(decoder_1_out11),
    .out12(decoder_1_out12), .out13(decoder_1_out13), .out14(decoder_1_out14), .out15(decoder_1_out15),
    .sel(Rd));  // open: en
  and and_1 (and_1_out, decoder_1_out0, write_Control);
  and and_2 (and_2_out, decoder_1_out1, write_Control);
  and and_3 (and_3_out, decoder_1_out2, write_Control);
  and and_4 (and_4_out, decoder_1_out3, write_Control);
  and and_5 (and_5_out, decoder_1_out4, write_Control);
  and and_6 (and_6_out, decoder_1_out5, write_Control);
  and and_7 (and_7_out, decoder_1_out6, write_Control);
  and and_8 (and_8_out, decoder_1_out7, write_Control);
  Register #(.width(16)) register_1 (.D(in_4), .en(and_1_out), .Q(register_1_q), .clk(Clk), .clr(Clear));
  Register #(.width(16)) register_2 (.D(in_4), .en(and_2_out), .Q(register_2_q), .clk(Clk), .clr(Clear));
  Register #(.width(16)) register_3 (.D(in_4), .en(and_3_out), .Q(register_3_q), .clk(Clk), .clr(Clear));
  Register #(.width(16)) register_4 (.D(in_4), .en(and_4_out), .Q(register_4_q), .clk(Clk), .clr(Clear));
  Register #(.width(16)) register_5 (.D(in_4), .en(and_5_out), .Q(register_5_q), .clk(Clk), .clr(Clear));
  Register #(.width(16)) register_6 (.D(in_4), .en(and_6_out), .Q(register_6_q), .clk(Clk), .clr(Clear));
  Register #(.width(16)) register_7 (.D(in_4), .en(and_7_out), .Q(register_7_q), .clk(Clk), .clr(Clear));
  Register #(.width(16)) register_8 (.D(in_4), .en(and_8_out), .Q(register_8_q), .clk(Clk), .clr(Clear));
  and and_9 (and_9_out, decoder_1_out8, write_Control);
  and and_10 (and_10_out, decoder_1_out9, write_Control);
  and and_11 (and_11_out, decoder_1_out10, write_Control);
  and and_12 (and_12_out, decoder_1_out11, write_Control);
  and and_13 (and_13_out, decoder_1_out12, write_Control);
  and and_14 (and_14_out, decoder_1_out13, write_Control);
  and and_15 (and_15_out, decoder_1_out14, write_Control);
  and and_16 (and_16_out, decoder_1_out15, write_Control);
  Register #(.width(16)) register_9 (.D(in_4), .en(and_9_out), .Q(register_9_q), .clk(Clk), .clr(Clear));
  Register #(.width(16)) register_10 (.D(in_4), .en(and_10_out), .Q(register_10_q), .clk(Clk), .clr(Clear));
  Register #(.width(16)) register_11 (.D(in_4), .en(and_11_out), .Q(register_11_q), .clk(Clk), .clr(Clear));
  Register #(.width(16)) register_12 (.D(in_4), .en(and_12_out), .Q(register_12_q), .clk(Clk), .clr(Clear));
  Register #(.width(16)) register_13 (.D(in_4), .en(and_13_out), .Q(register_13_q), .clk(Clk), .clr(Clear));
  Register #(.width(16)) register_14 (.D(in_4), .en(and_14_out), .Q(register_14_q), .clk(Clk), .clr(Clear));
  Register #(.width(16)) register_15 (.D(in_4), .en(and_15_out), .Q(register_15_q), .clk(Clk), .clr(Clear));
  Register #(.width(16)) register_16 (.D(in_4), .en(and_16_out), .Q(register_16_q), .clk(Clk), .clr(Clear));
  Multiplexer #(.select(4), .width(16)) multiplexer_1 (
    .in0(register_1_q), .in1(register_2_q), .in2(register_3_q), .in3(register_4_q), .in4(register_5_q),
    .in5(register_6_q), .in6(register_7_q), .in7(register_8_q), .in8(register_9_q), .in9(register_10_q),
    .in10(register_11_q), .in11(register_12_q), .in12(register_13_q), .in13(register_14_q),
    .in14(register_15_q), .in15(register_16_q), .out(out_8), .sel(Rs));  // open: en
  Multiplexer #(.select(4), .width(16)) multiplexer_2 (
    .in0(register_1_q), .in1(register_2_q), .in2(register_3_q), .in3(register_4_q), .in4(register_5_q),
    .in5(register_6_q), .in6(register_7_q), .in7(register_8_q), .in8(register_9_q), .in9(register_10_q),
    .in10(register_11_q), .in11(register_12_q), .in12(register_13_q), .in13(register_14_q),
    .in14(register_15_q), .in15(register_16_q), .out(out_9), .sel(Rt));  // open: en

  // Notes on the sheet:
  //   Write Data
  //   R0
  //   R1
  //   R2
  //   R3
  //   R4
  //   R5
  //   R6
  //   R7
  //   R8
  //   R9
  //   R10
  //   R11
  //   R12
  //   R13
  //   R14
  //   R15
  //   Read Data 1
  //   Read Data 2
endmodule

module _1_bit_ALU (
  input  A,
  input  B,
  input  Cin,
  input  [1:0] ALU_Select,
  output Result,
  output Cout
);

  wire adder_1_out, and_1_out, multiplexer_1_out, not_1_out, or_1_out;

  not not_1 (not_1_out, B);
  and and_1 (and_1_out, A, B);
  or or_1 (or_1_out, A, B);
  Multiplexer multiplexer_1 (.in0(B), .in1(not_1_out), .out(multiplexer_1_out), .sel(ALU_Select[0]));  // open: en
  Adder #(.width(1)) adder_1 (.a(A), .b(multiplexer_1_out), .out(adder_1_out), .cin(Cin), .cout(Cout));
  Multiplexer #(.select(2)) multiplexer_2 (
    .in0(and_1_out), .in1(or_1_out), .in2(adder_1_out), .in3(adder_1_out), .out(Result), .sel(ALU_Select));  // open: en

  // Notes on the sheet:
  //   B/B
endmodule

module _16_bit_ALU (
  input  Cin,
  input  [15:0] A,
  input  [15:0] B,
  input  [1:0] ALU_Select,
  output [15:0] Result,
  output Zero_Flag,
  output Cout,
  output Over_Flow
);

  wire n1_bit_alu_1_cout, n1_bit_alu_2_cout, n1_bit_alu_3_cout, n1_bit_alu_4_cout, n1_bit_alu_5_cout,
       n1_bit_alu_6_cout, n1_bit_alu_7_cout, n1_bit_alu_8_cout, n1_bit_alu_9_cout, n1_bit_alu_10_cout,
       n1_bit_alu_11_cout, n1_bit_alu_12_cout, n1_bit_alu_13_cout, n1_bit_alu_14_cout, n1_bit_alu_15_cout;

  Comparator #(.width(16)) comparator_1 (.a(A), .b(B), .eq(Zero_Flag));  // open: gt, lt
  _1_bit_ALU u_1_bit_alu_1 (
    .ALU_Select(ALU_Select), .Result(Result[0]), .Cout(n1_bit_alu_1_cout), .A(A[0]), .B(B[0]), .Cin(Cin));
  _1_bit_ALU u_1_bit_alu_2 (
    .ALU_Select(ALU_Select), .Result(Result[1]), .Cout(n1_bit_alu_2_cout), .A(A[1]), .B(B[1]),
    .Cin(n1_bit_alu_1_cout));
  _1_bit_ALU u_1_bit_alu_3 (
    .ALU_Select(ALU_Select), .Result(Result[2]), .Cout(n1_bit_alu_3_cout), .A(A[2]), .B(B[2]),
    .Cin(n1_bit_alu_2_cout));
  _1_bit_ALU u_1_bit_alu_4 (
    .ALU_Select(ALU_Select), .Result(Result[3]), .Cout(n1_bit_alu_4_cout), .A(A[3]), .B(B[3]),
    .Cin(n1_bit_alu_3_cout));
  _1_bit_ALU u_1_bit_alu_5 (
    .ALU_Select(ALU_Select), .Result(Result[4]), .Cout(n1_bit_alu_5_cout), .A(A[4]), .B(B[4]),
    .Cin(n1_bit_alu_4_cout));
  _1_bit_ALU u_1_bit_alu_6 (
    .ALU_Select(ALU_Select), .Result(Result[5]), .Cout(n1_bit_alu_6_cout), .A(A[5]), .B(B[5]),
    .Cin(n1_bit_alu_5_cout));
  _1_bit_ALU u_1_bit_alu_7 (
    .ALU_Select(ALU_Select), .Result(Result[6]), .Cout(n1_bit_alu_7_cout), .A(A[6]), .B(B[6]),
    .Cin(n1_bit_alu_6_cout));
  _1_bit_ALU u_1_bit_alu_8 (
    .ALU_Select(ALU_Select), .Result(Result[7]), .Cout(n1_bit_alu_8_cout), .A(A[7]), .B(B[7]),
    .Cin(n1_bit_alu_7_cout));
  _1_bit_ALU u_1_bit_alu_9 (
    .ALU_Select(ALU_Select), .Result(Result[8]), .Cout(n1_bit_alu_9_cout), .A(A[8]), .B(B[8]),
    .Cin(n1_bit_alu_8_cout));
  _1_bit_ALU u_1_bit_alu_10 (
    .ALU_Select(ALU_Select), .Result(Result[9]), .Cout(n1_bit_alu_10_cout), .A(A[9]), .B(B[9]),
    .Cin(n1_bit_alu_9_cout));
  _1_bit_ALU u_1_bit_alu_11 (
    .ALU_Select(ALU_Select), .Result(Result[10]), .Cout(n1_bit_alu_11_cout), .A(A[10]), .B(B[10]),
    .Cin(n1_bit_alu_10_cout));
  _1_bit_ALU u_1_bit_alu_12 (
    .ALU_Select(ALU_Select), .Result(Result[11]), .Cout(n1_bit_alu_12_cout), .A(A[11]), .B(B[11]),
    .Cin(n1_bit_alu_11_cout));
  _1_bit_ALU u_1_bit_alu_13 (
    .ALU_Select(ALU_Select), .Result(Result[12]), .Cout(n1_bit_alu_13_cout), .A(A[12]), .B(B[12]),
    .Cin(n1_bit_alu_12_cout));
  _1_bit_ALU u_1_bit_alu_14 (
    .ALU_Select(ALU_Select), .Result(Result[13]), .Cout(n1_bit_alu_14_cout), .A(A[13]), .B(B[13]),
    .Cin(n1_bit_alu_13_cout));
  _1_bit_ALU u_1_bit_alu_15 (
    .ALU_Select(ALU_Select), .Result(Result[14]), .Cout(n1_bit_alu_15_cout), .A(A[14]), .B(B[14]),
    .Cin(n1_bit_alu_14_cout));
  _1_bit_ALU u_1_bit_alu_16 (
    .ALU_Select(ALU_Select), .Result(Result[15]), .Cout(Cout), .A(A[15]), .B(B[15]), .Cin(n1_bit_alu_15_cout));
  xor xor_1 (Over_Flow, n1_bit_alu_15_cout, Cout);
endmodule

module R_Type (
  input  Cin,
  input  WC,
  input  [1:0] ALU_Sel,
  input  Clear,
  input  [3:0] in_5,
  input  [15:0] in_6,
  input  in_7,
  input  in_8,
  output out_9,
  output out_10,
  output Cout
);

  wire clock_1_out, clock_2_out;
  wire [15:0] adder_1_out, n16_bit_alu_1_result, n16_bit_register_1_out_8, n16_bit_register_1_out_9, PC_q,
       rom_1_data;

  Clock clock_1 (.out(clock_1_out));
  Register #(.width(16)) PC (.D(adder_1_out), .Q(PC_q), .clk(clock_1_out));  // open: en, clr
  Adder #(.width(16)) adder_1 (.a(PC_q), .b(16'h1), .out(adder_1_out), .cin(1'b0));  // open: cout
  Clock clock_2 (.out(clock_2_out));
  ROM #(.addrWidth(16), .dataWidth(16)) rom_1 (.addr(PC_q), .data(rom_1_data));  // open: sel
  _16_bit_Register u_16_bit_register_1 (
    .Rs(rom_1_data[11:8]), .Rt(rom_1_data[7:4]), .Rd(rom_1_data[3:0]), .in_4(n16_bit_alu_1_result),
    .write_Control(WC), .out_8(n16_bit_register_1_out_8), .out_9(n16_bit_register_1_out_9), .Clear(Clear),
    .Clk(clock_1_out));
  _16_bit_ALU u_16_bit_alu_1 (
    .Cin(Cin), .ALU_Select(ALU_Sel), .Cout(Cout), .B(n16_bit_register_1_out_9), .A(n16_bit_register_1_out_8),
    .Result(n16_bit_alu_1_result), .Zero_Flag(out_9), .Over_Flow(out_10));

  // Notes on the sheet:
  //   Adder
  //   contents of rom_1 (hex, n*v repeats v):
  //   123
  //   Ins. Memory
  //   Rd
  //   Rt
  //   Rs
  //   Opcode
  //   Register
endmodule

module Complete_DataPath (
  input  Cin,
  input  Mem__to_Reg,
  input  WC,
  input  Store,
  input  Reg__Dest,
  input  Clear,
  input  Load,
  input  ALU_Src,
  input  Mem__Clr,
  input  [1:0] ALU_Sel,
  output out_11,
  output out_12,
  output Cout
);

  wire clock_1_out;
  wire [3:0] multiplexer_1_out;
  wire [15:0] adder_1_out, bit_extender_1_out, multiplexer_2_out, multiplexer_3_out, n16_bit_alu_1_result,
       n16_bit_register_1_out_8, n16_bit_register_1_out_9, PC_q, ram_1_data, rom_1_data;

  Clock clock_1 (.out(clock_1_out));
  Register #(.width(16)) PC (.D(adder_1_out), .Q(PC_q), .clk(clock_1_out));  // open: en, clr
  Adder #(.width(16)) adder_1 (.a(PC_q), .b(16'h1), .out(adder_1_out), .cin(1'b0));  // open: cout
  ROM #(.addrWidth(16), .dataWidth(16)) rom_1 (.addr(PC_q), .data(rom_1_data));  // open: sel
  Multiplexer #(.width(4)) multiplexer_1 (
    .in0(rom_1_data[3:0]), .in1(rom_1_data[7:4]), .out(multiplexer_1_out), .sel(Reg__Dest));  // open: en
  assign bit_extender_1_out = {{12{1'b0}}, rom_1_data[3:0]};  // Bit_Extender bit_extender_1
  _16_bit_Register u_16_bit_register_1 (
    .Rs(rom_1_data[11:8]), .Rt(rom_1_data[7:4]), .Rd(multiplexer_1_out), .in_4(multiplexer_3_out),
    .write_Control(WC), .out_8(n16_bit_register_1_out_8), .out_9(n16_bit_register_1_out_9), .Clear(Clear),
    .Clk(clock_1_out));
  Multiplexer #(.width(16)) multiplexer_2 (
    .in0(n16_bit_register_1_out_9), .in1(bit_extender_1_out), .out(multiplexer_2_out), .sel(ALU_Src));  // open: en
  _16_bit_ALU u_16_bit_alu_1 (
    .Cin(Cin), .ALU_Select(ALU_Sel), .Cout(Cout), .B(multiplexer_2_out), .A(n16_bit_register_1_out_8),
    .Result(n16_bit_alu_1_result), .Zero_Flag(out_11), .Over_Flow(out_12));
  RAM #(.addrWidth(16), .dataWidth(16), .bus("separate")) ram_1 (
    .addr(n16_bit_alu_1_result), .din(n16_bit_register_1_out_9), .data(ram_1_data), .str(Store),
    .clk(clock_1_out), .ld(Load), .clr(Mem__Clr));  // open: sel
  Multiplexer #(.width(16)) multiplexer_3 (
    .in0(n16_bit_alu_1_result), .in1(ram_1_data), .out(multiplexer_3_out), .sel(Mem__to_Reg));  // open: en

  // Notes on the sheet:
  //   Adder
  //   Ins. Memory
  //   / Immediate
  //   Rd
  //   Rt
  //   Rs
  //   Opcode
  //   Register
  //   Data Memory
endmodule
