// Logisim project 24 bit MIPS Architechture.circ as structural Verilog: 6 circuits, main circuit main
module main (
  input  in_1,
  input  [4:0] in_2,
  input  [4:0] in_3,
  input  in_4,
  input  [4:0] in_5,
  input  in_6,
  input  [23:0] in_7,
  input  [2:0] in_8,
  input  in_9,
  input  in_10,
  input  [23:0] in_11,
  input  [3:0] in_12,
  input  [23:0] in_13,
  input  [2:0] in_14,
  output [23:0] out_15,
  output [23:0] out_16,
  output out_17,
  output out_18,
  output [23:0] out_19,
  output out_20,
  output out_21,
  output out_22
);

  wire clock_1_out;

  Control_Unit control_unit_1 (.OPCODE(in_12));  // open: ALU_COntrol, Cin, Reg__Dest, ALU_Src, WC, Load, Store, MEMEn, BEQ, JMP, MemToReg, in_1
  Clock clock_1 (.out(clock_1_out));
  _24_bit_Register u_24_bit_register_1 (
    .Rd(in_5), .Rs(in_2), .Rt(in_3), .Write_Data(in_7), .Write_Control(in_9), .CLR(in_10),
    .Read_Data_2(out_16), .Read_Data_1(out_15), .CLK(clock_1_out));
  _24_bit_ALU u_24_bit_alu_1 (
    .Zero_Flag(out_20), .Overflow(out_21), .B(in_13), .A(in_11), .out_6(out_19), .ALU_Control(in_14),
    .Cout(out_22));  // open: Cin, in_5
  _1_bit_ALU u_1_bit_alu_1 (
    .ALU_Control(in_8), .ALU_Out(out_17), .A(in_4), .B(in_6), .Out(out_18), .In(in_1));  // open: in_4
endmodule

module _24_bit_Register (
  input  [4:0] Rd,
  input  [4:0] Rs,
  input  [4:0] Rt,
  input  [23:0] Write_Data,
  input  Write_Control,
  input  CLK,
  input  CLR,
  output [23:0] Read_Data_2,
  output [23:0] Read_Data_1
);

  wire and_1_out, and_2_out, and_3_out, and_4_out, and_5_out, and_6_out, and_7_out, and_8_out, and_9_out,
       and_10_out, and_11_out, and_12_out, and_13_out, and_14_out, and_15_out, and_16_out, and_17_out,
       and_18_out, and_19_out, and_20_out, and_21_out, and_22_out, and_23_out, and_24_out, decoder_1_out0,
       decoder_1_out1, decoder_1_out2, decoder_1_out3, decoder_1_out4, decoder_1_out5, decoder_1_out6,
       decoder_1_out7, decoder_1_out8, decoder_1_out9, decoder_1_out10, decoder_1_out11, decoder_1_out12,
       decoder_1_out13, decoder_1_out14, decoder_1_out15, decoder_1_out16, decoder_1_out17, decoder_1_out18,
       decoder_1_out19, decoder_1_out20, decoder_1_out21, decoder_1_out22, decoder_1_out23;
  wire [23:0] R0_q, R1_q, R2_q, R3_q, R4_q, R5_q, R6_q, R7_q, R8_q, R9_q, R10_q, R11_q, R12_q, R13_q, R14_q,
       R15_q, R16_q, R17_q, R18_q, R19_q, R20_q, R21_q, R22_q, R23_q;

  Decoder #(.select(5)) decoder_1 (
    .out0(decoder_1_out0), .out1(decoder_1_out1), .out2(decoder_1_out2), .out3(decoder_1_out3),
    .out4(decoder_1_out4), .out5(decoder_1_out5), .out6(decoder_1_out6), .out7(decoder_1_out7),
    .out8(decoder_1_out8), .out9(decoder_1_out9), .out10(decoder_1_out10), .out11(decoder_1_out11),
    .out12(decoder_1_out12), .out13(decoder_1_out13), .out14(decoder_1_out14), .out15(decoder_1_out15),
    .out16(decoder_1_out16), .out17(decoder_1_out17), .out18(decoder_1_out18), .out19(decoder_1_out19),
    .out20(decoder_1_out20), .out21(decoder_1_out21), .out22(decoder_1_out22), .out23(decoder_1_out23),
    .sel(Rd));  // open: out24, out25, out26, out27, out28, out29, out30, out31, en
  and and_1 (and_1_out, decoder_1_out0, Write_Control);
  and and_2 (and_2_out, decoder_1_out1, Write_Control);
  and and_3 (and_3_out, decoder_1_out2, Write_Control);
  and and_4 (and_4_out, decoder_1_out3, Write_Control);
  and and_5 (and_5_out, decoder_1_out4, Write_Control);
  and and_6 (and_6_out, decoder_1_out5, Write_Control);
  and and_7 (and_7_out, decoder_1_out6, Write_Control);
  and and_8 (and_8_out, decoder_1_out7, Write_Control);
  and and_9 (and_9_out, decoder_1_out8, Write_Control);
  and and_10 (and_10_out, decoder_1_out9, Write_Control);
  and and_11 (and_11_out, decoder_1_out10, Write_Control);
  and and_12 (and_12_out, decoder_1_out11, Write_Control);
  Register #(.width(24)) R0 (.D(Write_Data), .en(and_1_out), .Q(R0_q), .clk(CLK), .clr(CLR));
  Register #(.width(24)) R1 (.D(Write_Data), .en(and_2_out), .Q(R1_q), .clk(CLK), .clr(CLR));
  Register #(.width(24)) R2 (.D(Write_Data), .en(and_3_out), .Q(R2_q), .clk(CLK), .clr(CLR));
  Register #(.width(24)) R3 (.D(Write_Data), .en(and_4_out), .Q(R3_q), .clk(CLK), .clr(CLR));
  Register #(.width(24)) R4 (.D(Write_Data), .en(and_5_out), .Q(R4_q), .clk(CLK), .clr(CLR));
  Register #(.width(24)) R5 (.D(Write_Data), .en(and_6_out), .Q(R5_q), .clk(CLK), .clr(CLR));
  Register #(.width(24)) R6 (.D(Write_Data), .en(and_7_out), .Q(R6_q), .clk(CLK), .clr(CLR));
  Register #(.width(24)) R7 (.D(Write_Data), .en(and_8_out), .Q(R7_q), .clk(CLK), .clr(CLR));
  Register #(.width(24)) R8 (.D(Write_Data), .en(and_9_out), .Q(R8_q), .clk(CLK), .clr(CLR));
  Register #(.width(24)) R9 (.D(Write_Data), .en(and_10_out), .Q(R9_q), .clk(CLK), .clr(CLR));
  Register #(.width(24)) R10 (.D(Write_Data), .en(and_11_out), .Q(R10_q), .clk(CLK), .clr(CLR));
  Register #(.width(24)) R11 (.D(Write_Data), .en(and_12_out), .Q(R11_q), .clk(CLK), .clr(CLR));
  and and_13 (and_13_out, decoder_1_out12, Write_Control);
  and and_14 (and_14_out, decoder_1_out13, Write_Control);
  and and_15 (and_15_out, decoder_1_out14, Write_Control);
  and and_16 (and_16_out, decoder_1_out15, Write_Control);
  and and_17 (and_17_out, decoder_1_out16, Write_Control);
  and and_18 (and_18_out, decoder_1_out17, Write_Control);
  and and_19 (and_19_out, decoder_1_out18, Write_Control);
  and and_20 (and_20_out, decoder_1_out19, Write_Control);
  and and_21 (and_21_out, decoder_1_out20, Write_Control);
  and and_22 (and_22_out, decoder_1_out21, Write_Control);
  and and_23 (and_23_out, decoder_1_out22, Write_Control);
  and and_24 (and_24_out, decoder_1_out23, Write_Control);
  Register #(.width(24)) R12 (.D(Write_Data), .en(and_13_out), .Q(R12_q), .clk(CLK), .clr(CLR));
  Register #(.width(24)) R13 (.D(Write_Data), .en(and_14_out), .Q(R13_q), .clk(CLK), .clr(CLR));
  Register #(.width(24)) R14 (.D(Write_Data), .en(and_15_out), .Q(R14_q), .clk(CLK), .clr(CLR));
  Register #(.width(24)) R15 (.D(Write_Data), .en(and_16_out), .Q(R15_q), .clk(CLK), .clr(CLR));
  Register #(.width(24)) R16 (.D(Write_Data), .en(and_17_out), .Q(R16_q), .clk(CLK), .clr(CLR));
  Register #(.width(24)) R17 (.D(Write_Data), .en(and_18_out), .Q(R17_q), .clk(CLK), .clr(CLR));
  Register #(.width(24)) R18 (.D(Write_Data), .en(and_19_out), .Q(R18_q), .clk(CLK), .clr(CLR));
  Register #(.width(24)) R19 (.D(Write_Data), .en(and_20_out), .Q(R19_q), .clk(CLK), .clr(CLR));
  Register #(.width(24)) R20 (.D(Write_Data), .en(and_21_out), .Q(R20_q), .clk(CLK), .clr(CLR));
  Register #(.width(24)) R21 (.D(Write_Data), .en(and_22_out), .Q(R21_q), .clk(CLK), .clr(CLR));
  Register #(.width(24)) R22 (.D(Write_Data), .en(and_23_out), .Q(R22_q), .clk(CLK), .clr(CLR));
  Register #(.width(24)) R23 (.D(Write_Data), .en(and_24_out), .Q(R23_q), .clk(CLK), .clr(CLR));
  Multiplexer #(.select(5), .width(24)) multiplexer_1 (
    .in0(R0_q), .in1(R1_q), .in2(R2_q), .in3(R3_q), .in4(R4_q), .in5(R5_q), .in6(R6_q), .in7(R7_q),
    .in8(R8_q), .in9(R9_q), .in10(R10_q), .in11(R11_q), .in12(R12_q), .in13(R13_q), .in14(R14_q),
    .in15(R15_q), .in16(R16_q), .in17(R17_q), .in18(R18_q), .in19(R19_q), .in20(R20_q), .in21(R21_q),
    .in22(R22_q), .in23(R23_q), .out(Read_Data_1), .sel(Rs));  // open: in24, in25, in26, in27, in28, in29, in30, in31, en
  Multiplexer #(.select(5), .width(24)) multiplexer_2 (
    .in0(R0_q), .in1(R1_q), .in2(R2_q), .in3(R3_q), .in4(R4_q), .in5(R5_q), .in6(R6_q), .in7(R7_q),
    .in8(R8_q), .in9(R9_q), .in10(R10_q), .in11(R11_q), .in12(R12_q), .in13(R13_q), .in14(R14_q),
    .in15(R15_q), .in16(R16_q), .in17(R17_q), .in18(R18_q), .in19(R19_q), .in20(R20_q), .in21(R21_q),
    .in22(R22_q), .in23(R23_q), .out(Read_Data_2), .sel(Rt));  // open: in24, in25, in26, in27, in28, in29, in30, in31, en
endmodule

module _1_bit_ALU (
  input  A,
  input  B,
  input  In,
  input  [1:0] in_4,
  input  [2:0] ALU_Control,
  output ALU_Out,
  output Out
);

  wire adder_1_out, and_1_out, bit_extender_1_out, comparator_1_lt, multiplexer_1_out, nor_1_out, not_1_out,
       shifter_1_out;

  Multiplexer multiplexer_1 (.in0(B), .in1(not_1_out), .out(multiplexer_1_out), .sel(ALU_Control[2]));  // open: en
  not not_1 (not_1_out, B);
  Bit_Extender #(.in_width(2), .out_width(1)) bit_extender_1 (.in(in_4), .out(bit_extender_1_out));
  Shifter #(.width(1)) shifter_1 (.in(A), .\dist (bit_extender_1_out), .out(shifter_1_out));
  Comparator #(.width(1)) comparator_1 (.a(A), .b(B), .lt(comparator_1_lt));  // open: gt, eq
  Adder #(.width(1)) adder_1 (.a(A), .b(multiplexer_1_out), .out(adder_1_out), .cin(In), .cout(Out));
  and and_1 (and_1_out, A, B);
  nor nor_1 (nor_1_out, A, B);
  Multiplexer #(.select(3)) multiplexer_2 (
    .in0(adder_1_out), .in1(and_1_out), .in2(shifter_1_out), .in3(nor_1_out), .in4(adder_1_out),
    .in5(comparator_1_lt), .in7(1'b0), .out(ALU_Out), .sel(ALU_Control));  // open: in6, en

  // Notes on the sheet:
  //   ADD
  //   AND
  //   SLL
  //   NOR
  //   SLT
  //   SUB
endmodule

module _24_bit_ALU (
  input  Cin,
  input  [23:0] A,
  input  [23:0] B,
  input  [2:0] ALU_Control,
  input  [1:0] in_5,
  output [23:0] out_6,
  output Zero_Flag,
  output Overflow,
  output Cout
);

  wire n1_bit_alu_1_out, n1_bit_alu_2_out, n1_bit_alu_3_out, n1_bit_alu_4_out, n1_bit_alu_5_out,
       n1_bit_alu_6_out, n1_bit_alu_7_out, n1_bit_alu_8_out, n1_bit_alu_9_out, n1_bit_alu_10_out,
       n1_bit_alu_11_out, n1_bit_alu_12_out, n1_bit_alu_13_out, n1_bit_alu_14_out, n1_bit_alu_15_out,
       n1_bit_alu_16_out, n1_bit_alu_17_out, n1_bit_alu_18_out, n1_bit_alu_19_out, n1_bit_alu_20_out,
       n1_bit_alu_21_out, n1_bit_alu_22_out, n1_bit_alu_23_out;

  Comparator #(.width(24)) comparator_1 (.a(A), .b(B), .eq(Zero_Flag));  // open: gt, lt
  _1_bit_ALU u_1_bit_alu_1 (
    .ALU_Control(ALU_Control), .ALU_Out(out_6[0]), .A(A[0]), .B(B[0]), .Out(n1_bit_alu_1_out), .In(Cin),
    .in_4(in_5));
  _1_bit_ALU u_1_bit_alu_2 (
    .ALU_Control(ALU_Control), .ALU_Out(out_6[1]), .A(A[1]), .B(B[1]), .Out(n1_bit_alu_2_out),
    .In(n1_bit_alu_1_out), .in_4(in_5));
  _1_bit_ALU u_1_bit_alu_3 (
    .ALU_Control(ALU_Control), .ALU_Out(out_6[2]), .A(A[2]), .B(B[2]), .Out(n1_bit_alu_3_out),
    .In(n1_bit_alu_2_out), .in_4(in_5));
  _1_bit_ALU u_1_bit_alu_4 (
    .ALU_Control(ALU_Control), .ALU_Out(out_6[3]), .A(A[3]), .B(B[3]), .Out(n1_bit_alu_4_out),
    .In(n1_bit_alu_3_out), .in_4(in_5));
  _1_bit_ALU u_1_bit_alu_5 (
    .ALU_Control(ALU_Control), .ALU_Out(out_6[4]), .A(A[4]), .B(B[4]), .Out(n1_bit_alu_5_out),
    .In(n1_bit_alu_4_out), .in_4(in_5));
  _1_bit_ALU u_1_bit_alu_6 (
    .ALU_Control(ALU_Control), .ALU_Out(out_6[5]), .A(A[5]), .B(B[5]), .Out(n1_bit_alu_6_out),
    .In(n1_bit_alu_5_out), .in_4(in_5));
  _1_bit_ALU u_1_bit_alu_7 (
    .ALU_Control(ALU_Control), .ALU_Out(out_6[6]), .A(A[6]), .B(B[6]), .Out(n1_bit_alu_7_out),
    .In(n1_bit_alu_6_out), .in_4(in_5));
  _1_bit_ALU u_1_bit_alu_8 (
    .ALU_Control(ALU_Control), .ALU_Out(out_6[7]), .A(A[7]), .B(B[7]), .Out(n1_bit_alu_8_out),
    .In(n1_bit_alu_7_out), .in_4(in_5));
  _1_bit_ALU u_1_bit_alu_9 (
    .ALU_Control(ALU_Control), .ALU_Out(out_6[8]), .A(A[8]), .B(B[8]), .Out(n1_bit_alu_9_out),
    .In(n1_bit_alu_8_out), .in_4(in_5));
  _1_bit_ALU u_1_bit_alu_10 (
    .ALU_Control(ALU_Control), .ALU_Out(out_6[9]), .A(A[9]), .B(B[9]), .Out(n1_bit_alu_10_out),
    .In(n1_bit_alu_9_out), .in_4(in_5));
  _1_bit_ALU u_1_bit_alu_11 (
    .ALU_Control(ALU_Control), .ALU_Out(out_6[10]), .A(A[10]), .B(B[10]), .Out(n1_bit_alu_11_out),
    .In(n1_bit_alu_10_out), .in_4(in_5));
  _1_bit_ALU u_1_bit_alu_12 (
    .ALU_Control(ALU_Control), .ALU_Out(out_6[11]), .A(A[11]), .B(B[11]), .Out(n1_bit_alu_12_out),
    .In(n1_bit_alu_11_out), .in_4(in_5));
  _1_bit_ALU u_1_bit_alu_13 (
    .ALU_Control(ALU_Control), .ALU_Out(out_6[12]), .A(A[12]), .B(B[12]), .Out(n1_bit_alu_13_out),
    .In(n1_bit_alu_12_out), .in_4(in_5));
  _1_bit_ALU u_1_bit_alu_14 (
    .ALU_Control(ALU_Control), .ALU_Out(out_6[13]), .A(A[13]), .B(B[13]), .Out(n1_bit_alu_14_out),
    .In(n1_bit_alu_13_out), .in_4(in_5));
  _1_bit_ALU u_1_bit_alu_15 (
    .ALU_Control(ALU_Control), .ALU_Out(out_6[14]), .A(A[14]), .B(B[14]), .Out(n1_bit_alu_15_out),
    .In(n1_bit_alu_14_out), .in_4(in_5));
  _1_bit_ALU u_1_bit_alu_16 (
    .ALU_Control(ALU_Control), .ALU_Out(out_6[15]), .A(A[15]), .B(B[15]), .Out(n1_bit_alu_16_out),
    .In(n1_bit_alu_15_out), .in_4(in_5));
  _1_bit_ALU u_1_bit_alu_17 (
    .ALU_Control(ALU_Control), .ALU_Out(out_6[16]), .A(A[16]), .B(B[16]), .Out(n1_bit_alu_17_out),
    .In(n1_bit_alu_16_out), .in_4(in_5));
  _1_bit_ALU u_1_bit_alu_18 (
    .ALU_Control(ALU_Control), .ALU_Out(out_6[17]), .A(A[17]), .B(B[17]), .Out(n1_bit_alu_18_out),
    .In(n1_bit_alu_17_out), .in_4(in_5));
  _1_bit_ALU u_1_bit_alu_19 (
    .ALU_Control(ALU_Control), .ALU_Out(out_6[18]), .A(A[18]), .B(B[18]), .Out(n1_bit_alu_19_out),
    .In(n1_bit_alu_18_out), .in_4(in_5));
  _1_bit_ALU u_1_bit_alu_20 (
    .ALU_Control(ALU_Control), .ALU_Out(out_6[19]), .A(A[19]), .B(B[19]), .Out(n1_bit_alu_20_out),
    .In(n1_bit_alu_19_out), .in_4(in_5));
  _1_bit_ALU u_1_bit_alu_21 (
    .ALU_Control(ALU_Control), .ALU_Out(out_6[20]), .A(A[20]), .B(B[20]), .Out(n1_bit_alu_21_out),
    .In(n1_bit_alu_20_out), .in_4(in_5));
  _1_bit_ALU u_1_bit_alu_22 (
    .ALU_Control(ALU_Control), .ALU_Out(out_6[21]), .A(A[21]), .B(B[21]), .Out(n1_bit_alu_22_out),
    .In(n1_bit_alu_21_out), .in_4(in_5));
  _1_bit_ALU u_1_bit_alu_23 (
    .ALU_Control(ALU_Control), .ALU_Out(out_6[22]), .A(A[22]), .B(B[22]), .Out(n1_bit_alu_23_out),
    .In(n1_bit_alu_22_out), .in_4(in_5));
  _1_bit_ALU u_1_bit_alu_24 (
    .ALU_Control(ALU_Control), .ALU_Out(out_6[23]), .A(A[23]), .B(B[23]), .Out(Cout), .In(n1_bit_alu_23_out),
    .in_4(in_5));
  xor xor_1 (Overflow, n1_bit_alu_23_out, Cout);
endmodule

module Control_Unit (
  input  [2:0] in_1,
  input  [3:0] OPCODE,
  output [2:0] ALU_COntrol,
  output Cin,
  output Reg__Dest,
  output ALU_Src,
  output WC,
  output Load,
  output Store,
  output MEMEn,
  output BEQ,
  output JMP,
  output MemToReg
);

  wire decoder_1_out0, decoder_1_out1, decoder_1_out2, decoder_1_out3, decoder_1_out4, decoder_1_out5,
       decoder_1_out6, or_1_out;
  wire [3:0] bit_extender_1_out, multiplexer_1_out;

  assign bit_extender_1_out = {{1{1'b0}}, in_1};  // Bit_Extender bit_extender_1
  or or_1 (or_1_out, OPCODE[3], OPCODE[2], OPCODE[1], OPCODE[0]);
  Multiplexer #(.width(4)) multiplexer_1 (
    .in0(bit_extender_1_out), .in1(OPCODE), .out(multiplexer_1_out), .sel(or_1_out));  // open: en
  Decoder #(.select(4)) decoder_1 (
    .out0(decoder_1_out0), .out1(decoder_1_out1), .out2(decoder_1_out2), .out3(decoder_1_out3),
    .out4(decoder_1_out4), .out5(decoder_1_out5), .out6(decoder_1_out6), .out7(Store), .out8(Load),
    .out9(BEQ), .out10(JMP), .sel(multiplexer_1_out));  // open: out11, out12, out13, out14, out15, en
  or or_2 (ALU_COntrol[2], decoder_1_out2, decoder_1_out4, decoder_1_out5, BEQ);
  or or_3 (ALU_COntrol[1], decoder_1_out1, decoder_1_out2, decoder_1_out3);
  or or_4 (ALU_COntrol[0], decoder_1_out0, decoder_1_out3, decoder_1_out5);
  or or_5 (Cin, decoder_1_out4, BEQ);
  or or_6 (Reg__Dest, decoder_1_out6, Store, Load, BEQ, JMP);
  or or_7 (ALU_Src, decoder_1_out6, Store, Load);
  or or_8 (WC, decoder_1_out0, decoder_1_out1, decoder_1_out3, decoder_1_out4, decoder_1_out5, decoder_1_out6, Load);
  or or_9 (MEMEn, Store, Load);

  assign MemToReg = Load;

  // Notes on the sheet:
  //   C
  //   B
  //   A
endmodule

module Complete_DataPath (
  input  in_1,
  input  in_2,
  input  in_3,
  output out_4,
  output out_5
);

  wire and_1_out, clock_1_out, control_unit_1_alu_src, control_unit_1_beq, control_unit_1_cin,
       control_unit_1_jmp, control_unit_1_load, control_unit_1_memen, control_unit_1_memtoreg,
       control_unit_1_reg__dest, control_unit_1_store, control_unit_1_wc, n24_bit_alu_1_zero_flag;
  wire [2:0] control_unit_1_alu_control;
  wire [4:0] multiplexer_1_out;
  wire [23:0] adder_1_out, adder_2_out, bit_extender_1_out, bit_extender_2_out, multiplexer_2_out,
       multiplexer_3_out, multiplexer_4_out, multiplexer_5_out, n24_bit_alu_1_out_6,
       n24_bit_register_1_read_data_1, n24_bit_register_1_read_data_2, PC_q, ram_1_data, rom_1_data,
       shifter_1_out;

  Clock clock_1 (.out(clock_1_out));
  Register #(.width(24)) PC (.D(multiplexer_4_out), .Q(PC_q), .clk(clock_1_out), .clr(in_1));  // open: en
  Adder #(.width(24)) adder_1 (.a(PC_q), .b(24'h1), .out(adder_1_out), .cin(1'b0));  // open: cout
  ROM #(.addrWidth(24), .dataWidth(24)) rom_1 (.addr(PC_q), .data(rom_1_data));  // open: sel
  assign bit_extender_1_out = {{14{1'b0}}, rom_1_data[9:0]};  // Bit_Extender bit_extender_1
  assign bit_extender_2_out = {{4{1'b0}}, rom_1_data[19:0]};  // Bit_Extender bit_extender_2
  Multiplexer #(.width(5)) multiplexer_1 (
    .in0(rom_1_data[9:5]), .in1(rom_1_data[14:10]), .out(multiplexer_1_out), .sel(control_unit_1_reg__dest));  // open: en
  _24_bit_Register u_24_bit_register_1 (
    .Rd(multiplexer_1_out), .Rs(rom_1_data[19:15]), .Rt(rom_1_data[14:10]), .Write_Data(multiplexer_5_out),
    .Write_Control(control_unit_1_wc), .CLR(in_3), .Read_Data_2(n24_bit_register_1_read_data_2),
    .Read_Data_1(n24_bit_register_1_read_data_1), .CLK(clock_1_out));
  Multiplexer #(.width(24)) multiplexer_2 (
    .in0(n24_bit_register_1_read_data_2), .in1(bit_extender_1_out), .out(multiplexer_2_out),
    .sel(control_unit_1_alu_src));  // open: en
  Shifter #(.width(24)) shifter_1 (.in(bit_extender_1_out), .\dist (5'b10000), .out(shifter_1_out));
  Control_Unit control_unit_1 (
    .OPCODE(rom_1_data[23:20]), .ALU_COntrol(control_unit_1_alu_control), .Cin(control_unit_1_cin),
    .Reg__Dest(control_unit_1_reg__dest), .ALU_Src(control_unit_1_alu_src), .WC(control_unit_1_wc),
    .Load(control_unit_1_load), .Store(control_unit_1_store), .MEMEn(control_unit_1_memen),
    .BEQ(control_unit_1_beq), .JMP(control_unit_1_jmp), .MemToReg(control_unit_1_memtoreg),
    .in_1(rom_1_data[2:0]));
  _24_bit_ALU u_24_bit_alu_1 (
    .Cin(control_unit_1_cin), .Zero_Flag(n24_bit_alu_1_zero_flag), .Overflow(out_4), .B(multiplexer_2_out),
    .A(n24_bit_register_1_read_data_1), .out_6(n24_bit_alu_1_out_6),
    .ALU_Control(control_unit_1_alu_control), .Cout(out_5), .in_5(rom_1_data[4:3]));
  Adder #(.width(24)) adder_2 (.a(adder_1_out), .b(shifter_1_out), .out(adder_2_out));  // open: cin, cout
  and and_1 (and_1_out, control_unit_1_beq, n24_bit_alu_1_zero_flag);
  Multiplexer #(.width(24)) multiplexer_3 (
    .in0(adder_1_out), .in1(adder_2_out), .out(multiplexer_3_out), .sel(and_1_out));  // open: en
  Multiplexer #(.width(24)) multiplexer_4 (
    .in0(multiplexer_3_out), .in1(bit_extender_2_out), .out(multiplexer_4_out), .sel(control_unit_1_jmp));  // open: en
  RAM #(.addrWidth(24), .dataWidth(24), .bus("separate")) ram_1 (
    .addr(n24_bit_alu_1_out_6), .din(n24_bit_register_1_read_data_2), .data(ram_1_data),
    .str(control_unit_1_store), .sel(control_unit_1_memen), .clk(clock_1_out), .ld(control_unit_1_load),
    .clr(in_2));
  Multiplexer #(.width(24)) multiplexer_5 (
    .in0(n24_bit_alu_1_out_6), .in1(ram_1_data), .out(multiplexer_5_out), .sel(control_unit_1_memtoreg));  // open: en

  // Notes on the sheet:
  //   Adder
  //   Ins. Memory
  //   Address
  //   Immediate
  //   Func.Bits
  //   Shift
  //   Rd
  //   Rt
  //   Rs
  //   Opcode
  //   Register
  //   Rs
  //   Rt
  //   Data Memory
endmodule
